# Fritzing sketch Suhu (saved by Fritzing 1.0.1rc)

parts:
  U1 = ESP32S-HiLetgo [part_number=ESP32S-HiLetgo]
  A1 = nozzle-bolt style thermocouple [package=THT]
  A2 = MAX6675 module [package=THT]
  Part1 = LCD1602-I2C

nets:
  N1: U1.GPIO6, A2.pin2, Part1.VCC
  N2: U1.GPIO7, A2.pin1, Part1.GND
  N3: U1.GPIO0, A2.pin3
  N4: U1.GPIO4, A2.pin4
  N5: U1.GPIO16, A2.pin5
  N6: U1.GPIO21, Part1.SDA
  N7: U1.GPIO22, Part1.SCL
  N8: A1.pin1, A2.pin7
  N9: A1.pin2, A2.pin6

custom parts:
  ESP32S-HiLetgo: HiLetgo ESP-WROOM-32 ESP32 ESP-32S Development Board 2.4GHz Dual-Mode WiFi + Bluetooth Dual Cores Microcontroller The ESP32 integrated with Antenna switches, RF Balun, power amplifiers, low-noise amplifiers, filters, and management modules, and the entire solution occupies the least area of PCB. 2.4 GHz Wi-Fi plus Bluetooth dual-mode chip, with TSMC Ultra-low power consumption 40nm technology,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
  nozzle-bolt style thermocouple: Generic nozzle-bolt style thermocouple.
  MAX6675 module: MAX6675 Module + K Type Thermocouple Sensor Temperature Degrees.
  LCD1602-I2C: A standard character display, usually with 2x16 characters. Comes in many colors with LCM1602 IIC attached.
