# Fritzing sketch Counter (saved by Fritzing 0.9.3b)
circuit board: 8.46667cm x 5.64444cm

parts:
  U1 = ESP32S-HiLetgo [part_number=ESP32S-HiLetgo]
  Part1 = LCD1602-I2C
  Mod1 = Full Size SD Card Module
  RTC1 = DS3231 AT24C32 Real Time Clock
  J1 = Infrared Proximity Sensor
  S1 = Momentary Switch [package=ksa_sealed_tac_switch]
  S2 = Momentary Switch [package=ksa_sealed_tac_switch]
  S3 = Momentary Switch [package=ksa_sealed_tac_switch]

nets:
  N1: U1.GPIO39, S1.1
  N2: U1.GPIO34, S2.1
  N3: U1.GPIO35, S3.1
  GND: U1.GND, Part1.GND, Mod1.pin_2, Mod1.pin_16, RTC1.GND, J1.GND
  N4: U1.VIN, Mod1.pin_6
  VCC: U1.GPIO6, Part1.VCC, RTC1.VCC
  N5: U1.GPIO5, Mod1.pin_7, Mod1.pin_8
  N6: U1.GPIO18, Mod1.pin_12
  N7: U1.GPIO19, Mod1.pin_14
  N8: U1.GPIO21, Part1.SDA, RTC1.SDA
  N9: U1.GPIO22, Part1.SCL, RTC1.SCL
  N10: U1.GPIO23, Mod1.pin_10
  N11: S1.4, S2.4

custom parts:
  ESP32S-HiLetgo: HiLetgo ESP-WROOM-32 ESP32 ESP-32S Development Board 2.4GHz Dual-Mode WiFi + Bluetooth Dual Cores Microcontroller The ESP32 integrated with Antenna switches, RF Balun, power amplifiers, low-noise amplifiers, filters, and management modules, and the entire solution occupies the least area of PCB. 2.4 GHz Wi-Fi plus Bluetooth dual-mode chip, with TSMC Ultra-low power consumption 40nm technology,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
  LCD1602-I2C: A standard character display, usually with 2x16 characters. Comes in many colors with LCM1602 IIC attached.
  Full Size SD Card Module: SD Card Module Slot Socket Reader For Arduino ARM MCU
  DS3231 AT24C32 Real Time Clock: Real-time clock basedo on chip DS3231, plus memory chip AT24C32 (32 Kb storage capacity). On-chip temperature sensor with an accuracy of ±3 ℃, I2C bus interface maximum speed: 400 kHz. Operating voltage: 3.3 V to 5.5 V with battery backup capabilities.
